# Fritzing sketch TelegramArduino (saved by Fritzing 0.9.3b)
breadboards: 1

parts:
  U1 = NodeMCU V1.0
  RHT1 = Humidity and Temperature Sensor RHT03
  R1 = Resistor [tolerance=±5% resistance=100 package="0402 [SMD]"]
  LED1 = smd LED [color="Blue (430nm)" package="1206 [SMD]"]
  R4 = Resistor [tolerance=±5% resistance=10k package=THT]  # not connected
  KY-1 = Keyes Relay [package=THT]
  Q1 = NPN-Transistor [package="TO92 [THT]"]
  R5 = Resistor [tolerance=±5% resistance=10k package=THT]
  R6 = Resistor [tolerance=±5% resistance=1k package=THT]

nets:
  N1: U1.D3, R1.Pin_1
  3V3: U1.3V3, RHT1.Vcc
  N2: U1.GND, LED1.cathode
  N3: U1.D5, RHT1.Data-signal
  N4: U1.D6, R5.Pin_1
  N5: R1.Pin_0, LED1.anode
  N6: KY-1.signal, Q1.E, R6.Pin_0
  N7: KY-1.power, R6.Pin_1
  N8: KY-1.ground, Q1.C
  N9: Q1.B, R5.Pin_0

notes:
  3.3v
  DHT11
  10k

custom parts:
  NodeMCU V1.0: ESP8266 based NodeMCU
  Keyes Relay: The Keyes 5V relay module is suitable for SCM development, home appliance control. It uses a 5V~12V TIL control signal which can control DC / AC signal.
